# Fritzing sketch fingerprint scanner sketch (saved by Fritzing 0.9.6b)
breadboards: 1

parts:
  Mod1 = Raspberry Pi Pico
  Fingerprint = sensor_biometrico

nets:
  N1: Mod1.pin_1, Fingerprint.RX
  N2: Mod1.pin_2, Fingerprint.TX
  N3: Mod1.pin_3, Mod1.pin_8, Mod1.pin_13, Mod1.pin_18, Mod1.pin_23, Mod1.pin_28, Mod1.pin_33, Mod1.pin_38, Mod1.pin_42, Fingerprint.GND
  N4: Mod1.pin_37, Fingerprint.VCC

custom parts:
  Raspberry Pi Pico: Raspberry Pi Pico. Based around the RP2040 microcontroller the Pico is a low cost microcontroller device bringing Raspberry Pi quality, cost, and easy of use to the microcontroller space. Jan 2021, Split part in to two versions: tht (this one) and SMD. This one will drill holes for a .1 in header in pcb to allow plugging in the module as well as providing pads to solder the module to the top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
  sensor_biometrico: Optical Fingerprint Sensor
